# Fritzing sketch Telemetry Main Board 1.0 (saved by Fritzing 0.9.3b)
circuit board: 5.44069cm x 5.22579cm
breadboards: 1

parts:
  Part1 = Adafruit AMG8833 8x8 GRID EYE
  Raspberry_Pi_1 = Raspberry Pi 3 [part_number=RPI-3-V1.2]
  Part2 = Adafruit BME280

nets:
  3V3: Part1.VIN, Raspberry_Pi_1.3v3, Raspberry_Pi_1.3V3
  GND: Part1.GND, Raspberry_Pi_1.GND, Part2.GND
  N1: Part1.SDA, Raspberry_Pi_1.GPIO2, Part2.SDI/SDA
  N2: Part1.SCL, Raspberry_Pi_1.GPIO3, Part2.SCK/SCL
  5V: Raspberry_Pi_1.5V, Part2.VIN

custom parts:
  Adafruit BME280: Bosch has stepped up their game with their new BME280 sensor, an environmental sensor with temperature, barometric pressure and humidity! This sensor is great for all sorts of weather/environmental sensing and can even be used in both I2C and SPI! This precision sensor from Bosch is the best low-cost sensing solution for measuring humidity with ±3% accuracy, barometric pressure with ±1 hPa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
