# Fritzing sketch Telemetry Main Board 2.5 (saved by Fritzing 0.9.3b)
circuit board: 5.80657cm x 4.49163cm
breadboards: 1

parts:
  Raspberry_Pi_1 = Raspberry Pi 3 [part_number=RPI-3-V1.2]
  JP1 = Header 4 [package=molex-1x4_lock]
  JP2 = Header 4 [package=molex-1x4_lock]
  JP3 = Header 4 [package=molex-1x4_lock]

nets:
  3V3: Raspberry_Pi_1.3v3, Raspberry_Pi_1.3V3, JP3.1
  N1: Raspberry_Pi_1.GPIO2, JP1.2, JP2.2, JP3.2
  N2: Raspberry_Pi_1.GPIO3, JP1.3, JP2.3, JP3.3
  N3: Raspberry_Pi_1.GND, JP1.4, JP2.4, JP3.4
  N4: Raspberry_Pi_1.5V, JP1.1, JP2.1
