# Fritzing sketch PCF8591 Board (saved by Fritzing 0.9.3b)
circuit board: 5.36693cm x 2.79301cm
breadboards: 1

parts:
  JP2 = Header 4 [package=molex-1x4_lock]
  JP3 = Header 4 [package=molex-1x4_lock]

nets:
  N1: JP2.1, JP3.1
  N2: JP2.2, JP3.3
  N3: JP2.3, JP3.4
  N4: JP2.4, JP3.2
