# Fritzing sketch AMG8833 Board v2 (saved by Fritzing 0.9.3b)
circuit board: 5.33482cm x 2.79621cm
breadboards: 1

parts:
  Part2 = Adafruit AMG8833 8x8 GRID EYE
  JP2 = Header 4 [package=molex-1x4_lock]

nets:
  N1: Part2.VIN, JP2.4
  N2: Part2.GND, JP2.1
  N3: Part2.SDA, JP2.3
  N4: Part2.SCL, JP2.2
