# Fritzing sketch BME280 Board v2 (saved by Fritzing 0.9.3b)
circuit board: 5.3322cm x 2.79565cm
breadboards: 1

parts:
  JP3 = Header 4 [package=molex-1x4_lock]
  Part3 = Adafruit BME280

nets:
  N1: JP3.1, Part3.GND
  N2: JP3.2, Part3.SCK/SCL
  N3: JP3.3, Part3.SDI/SDA
  N4: JP3.4, Part3.VIN

custom parts:
  Adafruit BME280: Bosch has stepped up their game with their new BME280 sensor, an environmental sensor with temperature, barometric pressure and humidity! This sensor is great for all sorts of weather/environmental sensing and can even be used in both I2C and SPI! This precision sensor from Bosch is the best low-cost sensing solution for measuring humidity with ±3% accuracy, barometric pressure with ±1 hPa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
